# Fritzing sketch autoTrafficLight (saved by Fritzing 0.9.3b)
breadboards: 1

parts:
  부품1 = Arduino Uno (Rev3) - ICSP
  LED1 = smd LED [color="Red (633nm)" package="1206 [SMD]"]
  LED2 = smd LED [color="Yellow (585nm)" package="1206 [SMD]"]
  LED3 = smd LED [color="Green (565nm)" package="1206 [SMD]"]
  R1 = Resistor [tolerance=±5% resistance=100 package=THT]
  R2 = Resistor [tolerance=±5% resistance=100 package=THT]
  R3 = Resistor [tolerance=±5% resistance=100 package=THT]
  R4 = Resistor [tolerance=±5% resistance=100 package=THT]
  R5 = Resistor [tolerance=±5% resistance=100 package=THT]
  R6 = Resistor [tolerance=±5% resistance=100 package=THT]

nets:
  N1: 부품1.D8, LED3.anode
  N2: 부품1.D12/MISO, LED2.anode
  N3: 부품1.D13/SCK, LED1.anode
  N4: 부품1.GND, R4.Pin_0, R5.Pin_0, R6.Pin_0
  N5: LED1.cathode, R1.Pin_1
  N6: LED2.cathode, R2.Pin_1
  N7: LED3.cathode, R3.Pin_1
  N8: R1.Pin_0, R4.Pin_1
  N9: R2.Pin_0, R5.Pin_1
  N10: R3.Pin_0, R6.Pin_1
