# Fritzing sketch 12장  7세그먼트 사용하기 참고자료 (saved by Fritzing 0.9.3b)
breadboards: 1

parts:
  부품1 = Arduino Uno (Rev3)
  LED1 = 7-SEGMENT-4DIGIT-YOUNGSUN [package=7-segment-4digit-youngsun-longpads]

nets:
  N1: 부품1.A0, LED1.DIG3
  N2: 부품1.A1, LED1.E
  N3: 부품1.A2, LED1.COL-A
  N4: 부품1.A3, LED1.D
  N5: 부품1.A4/SDA, LED1.DIG2
  N6: 부품1.A5/SCL, LED1.DIG1
  N7: 부품1.D2, LED1.B
  N8: 부품1.D3_PWM, LED1.G
  N9: 부품1.D4, LED1.A
  N10: 부품1.D5_PWM, LED1.C
  N11: 부품1.D6_PWM, LED1.COL-C
  N12: 부품1.D7, LED1.F
