# Fritzing sketch catchSound (saved by Fritzing 0.9.3b)
breadboards: 1

parts:
  부품1 = Arduino Uno (Rev3)
  부품2 = Breakout Board for Electret Microphone
  LED1 = LED - 5mm [color="Yellow (592nm)" package="5 mm [THT]"]

nets:
  N1: 부품1.A0, 부품2.AUD
  N2: 부품1.D11_PWM/MOSI, LED1.anode
  GND: 부품1.GND, 부품2.GND, LED1.cathode
  5V: 부품1.5V, 부품2.VCC
