# Fritzing sketch piezoMusic (saved by Fritzing 0.9.3b)
breadboards: 1

parts:
  부품1 = Arduino Uno (Rev3) - ICSP
  J1 = Piezo Speaker
  R1 = Rotary Potentiometer (Small) [maximum_resistance=100kΩ package=THT]

nets:
  N1: 부품1.A0, R1.wiper
  N2: 부품1.D8, J1.pin2
  N3: 부품1.5V, R1.leg1
  N4: 부품1.GND, J1.pin1, R1.leg2
