# Fritzing sketch manualTrafficLight (saved by Fritzing 0.9.3b)
breadboards: 1

parts:
  부품1 = Arduino Uno (Rev3) - ICSP
  LED1 = smd LED [color="Red (633nm)" package="1206 [SMD]"]
  LED2 = smd LED [color="Yellow (585nm)" package="1206 [SMD]"]
  LED3 = smd LED [color="Green (565nm)" package="1206 [SMD]"]
  R1 = Resistor [tolerance=±5% resistance=100 package=THT]
  R2 = Resistor [tolerance=±5% resistance=100 package=THT]
  R3 = Resistor [tolerance=±5% resistance=100 package=THT]
  R4 = Resistor [tolerance=±5% resistance=100 package=THT]
  R5 = Resistor [tolerance=±5% resistance=100 package=THT]
  R6 = Resistor [tolerance=±5% resistance=100 package=THT]  # not connected
  S1 = Pushbutton [package="[THT]"]
  S2 = Pushbutton [package="[THT]"]
  S3 = Pushbutton [package="[THT]"]
  R7 = Resistor [tolerance=±5% resistance=10k package=THT]
  R8 = Resistor [tolerance=±5% resistance=10k package=THT]
  R9 = Resistor [tolerance=±5% resistance=10k package=THT]

nets:
  N1: 부품1.D2, S2.Pin_3, S2.Pin_4, R9.Pin_1
  N2: 부품1.D4, S3.Pin_3, S3.Pin_4, R8.Pin_1
  N3: 부품1.D7, S1.Pin_3, S1.Pin_4, R7.Pin_1
  N4: 부품1.GND, R3.Pin_1, R4.Pin_0, S1.Pin_1, S1.Pin_2, S2.Pin_1, S2.Pin_2, S3.Pin_1, S3.Pin_2
  N5: LED1.anode, LED2.cathode
  N6: LED3.cathode, LED3.anode
  N7: R1.Pin_0, R2.Pin_0, R3.Pin_0, R7.Pin_0, R8.Pin_0, R9.Pin_0
  N8: R1.Pin_1, R5.Pin_0
