# Fritzing sketch distanceLight (saved by Fritzing 0.9.3b)
breadboards: 1

parts:
  부품1 = Arduino Uno (Rev3)
  hc-sr1 = hc-sr04
  S1 = Pushbutton [package="[SMD]"]
  R1 = Resistor [tolerance=±5% resistance=10k package="0603 [SMD]"]
  R2 = Resistor [tolerance=±5% resistance=100 package="0603 [SMD]"]
  R3 = Resistor [tolerance=±5% resistance=100 package="0603 [SMD]"]
  LED1 = LED - 3mm [color="Red (633nm)" package="3 mm [THT]"]
  LED2 = LED - 3mm [color="Green (570nm)" package="3 mm [THT]"]
  R4 = Resistor [tolerance=±5% resistance=100 package="0603 [SMD]"]
  R5 = Resistor [tolerance=±5% resistance=100 package="0603 [SMD]"]

nets:
  N1: 부품1.D8, LED1.anode
  N2: 부품1.D9_PWM, LED2.anode
  N3: 부품1.D13/SCK, S1.Pin_3, S1.Pin_4, R1.Pin_1
  GND: 부품1.GND, hc-sr1.GND, R1.Pin_0, R2.Pin_0, R4.Pin_0
  N4: 부품1.D2, hc-sr1.Trig
  N5: 부품1.D3_PWM, hc-sr1.Echo
  5V: 부품1.5V, hc-sr1.VCC, S1.Pin_1, S1.Pin_2
  N6: R2.Pin_1, R3.Pin_0
  N7: R3.Pin_1, LED1.cathode
  N8: LED2.cathode, R5.Pin_1
  N9: R4.Pin_1, R5.Pin_0
