# Fritzing sketch musicPlayer (saved by Fritzing 0.9.3b)
breadboards: 1

parts:
  부품1 = Arduino Uno (Rev3) - ICSP
  J1 = Piezo Speaker
  S1 = Momentary Switch [package=ksa_sealed_tac_switch]
  S2 = Momentary Switch [package=ksa_sealed_tac_switch]
  R1 = Resistor [tolerance=±5% resistance=10k package="0805 [SMD]"]
  R2 = Resistor [tolerance=±5% resistance=10k package="0805 [SMD]"]

nets:
  N1: 부품1.D8, J1.pin2
  N2: 부품1.D12/MISO, 부품1.D13/SCK, 부품1.GND, J1.pin1, R1.Pin_0, R2.Pin_0
  N3: 부품1.5V, S1.2, S2.2
  N4: S1.4, R1.Pin_1
  N5: S2.4, R2.Pin_1
